// Logisim project ee.circ as structural Verilog: 1 circuit, main circuit main
module main (
);

  wire switch_1_p2, switch_2_p2, switch_3_p2, switch_4_p2, switch_5_p2, switch_6_p2, switch_6_p3,
       transistor_1_out, transistor_2_out, transistor_3_out, transistor_4_out, transistor_5_out,
       transistor_6_out, transistor_8_out, transistor_9_out;

  // Switch switch_1: pin names not known; wires that end beside it: 1'b1, switch_1_p2
  // Switch switch_2: pin names not known; wires that end beside it: 1'b1, switch_2_p2
  // Switch switch_3: pin names not known; wires that end beside it: 1'b1, switch_3_p2
  // Switch switch_4: pin names not known; wires that end beside it: 1'b1, switch_4_p2
  Transistor transistor_1 (.in(switch_4_p2), .out(transistor_1_out), .gate(switch_1_p2));
  Transistor transistor_2 (.in(switch_4_p2), .out(transistor_2_out), .gate(switch_2_p2));
  Transistor transistor_3 (.in(switch_4_p2), .out(transistor_3_out), .gate(switch_3_p2));
  // Switch switch_5: pin names not known; wires that end beside it: 1'b1, switch_5_p2
  Transistor transistor_4 (.in(switch_5_p2), .out(transistor_4_out), .gate(switch_1_p2));
  Transistor transistor_5 (.in(switch_5_p2), .out(transistor_5_out), .gate(switch_2_p2));
  Transistor transistor_6 (.in(switch_5_p2), .out(transistor_6_out), .gate(switch_3_p2));
  // Switch switch_6: pin names not known; wires that end beside it: 1'b1, switch_6_p2, switch_6_p3, transistor_4_out, transistor_1_out, 1'b0, 1'b0, 1'b0
  Transistor transistor_7 (.in(switch_6_p2), .out(switch_6_p3), .gate(switch_1_p2));
  Transistor transistor_8 (.in(switch_6_p2), .out(transistor_8_out), .gate(switch_2_p2));
  Transistor transistor_9 (.in(switch_6_p2), .out(transistor_9_out), .gate(switch_3_p2));
endmodule
